# Fritzing sketch circuit_diagram (saved by Fritzing 0.9.3b)
breadboards: 1

parts:
  - = Arduino Uno (Rev3)
  B2 = Photocell (LDR) [package=THT]
  B1 = Photocell (LDR) [package=THT]
  R1 = Resistor [tolerance=±5% resistance=1k package=THT]
  R3 = Resistor [tolerance=±5% resistance=1k package=THT]
  P1 = LED - 5mm [color="Infrared (880nm)" package="5 mm [THT]"]
  P3 = RGB LED (com. cathode, rgb) [package="5 mm [THT]"]
  R4 = Resistor [tolerance=±5% resistance=220 package=THT]
  R2 = Resistor [tolerance=±5% resistance=220 package=THT]
  R7 = Resistor [tolerance=±5% resistance=220 package=THT]
  R5 = Resistor [tolerance=±5% resistance=220 package=THT]
  R6 = Resistor [tolerance=±5% resistance=220 package=THT]
  T2 = X113647 Stepper Driver Board [package=board]
  M2 = 28BYJ-48 Stepper Motor
  T1 = X113647 Stepper Driver Board [package=board]
  M1 = 28BYJ-48 Stepper Motor
  P2 = LED - 5mm [color="Infrared (880nm)" package="5 mm [THT]"]
  B3 = Grove Light Sensor

nets:
  N1: -.A0, B2.pin_0, R3.Pin_1
  N2: -.A1, B1.pin_0, R1.Pin_1
  N3: -.A2, B3.SIG
  N4: -.D8, T1.IN4
  N5: -.D9_PWM, T2.IN1
  N6: -.D10_PWM/SS, T2.IN2
  N7: -.D11_PWM/MOSI, T2.IN3
  N8: -.D12/MISO, T2.IN4
  GND: -.GND, B2.pin_1, B1.pin_1, P1.cathode, P3.common_cathode, T2.GND, T1.GND, P2.cathode, B3.GND
  N9: -.D2, R7.Pin_1
  N10: -.D3_PWM, R6.Pin_1
  N11: -.D4, R5.Pin_1
  N12: -.D5_PWM, T1.IN1
  N13: -.D6_PWM, T1.IN2
  N14: -.D7, T1.IN3
  5V: -.5V, R1.Pin_0, R3.Pin_0, R4.Pin_0, R2.Pin_0, T2.+V, T1.+V, B3.VCC
  N15: P1.anode, R2.Pin_1
  N16: P3.red_anode, R5.Pin_0
  N17: P3.green_anode, R6.Pin_0
  N18: P3.blue_anode, R7.Pin_0
  N19: R4.Pin_1, P2.anode
  N20: T2.BLUE, M2.BLUE
  N21: T2.PINK, M2.PINK
  N22: T2.YELLOW, M2.YELLOW
  N23: T2.ORANGE, M2.ORANGE
  N24: T2.RED, M2.RED
  N25: T1.BLUE, M1.BLUE
  N26: T1.PINK, M1.PINK
  N27: T1.YELLOW, M1.YELLOW
  N28: T1.ORANGE, M1.ORANGE
  N29: T1.RED, M1.RED

notes:
  Kennzeichnungen nach DIN EN 81346-2:2010

custom parts:
  X113647 Stepper Driver Board: A common stepper motor driver board based on ULN2003APG darlington array
